# Fritzing sketch Using the stepper mottor (saved by Fritzing 0.8.7b)
breadboards: 1

parts:
  MOTOR1 = 28BYJ-48 Stepper Motor
  BREAKOUT1 = ULN2003A breakout board
  Part1 = Arduino Uno (Rev3)
  U1 = POT [package=pot_alpha_rv16af-20]
  VCC1 = Battery block 9V

nets:
  N1: MOTOR1.RED, BREAKOUT1.RED_wire
  N2: MOTOR1.ORANGE, BREAKOUT1.ORANGE_wire
  N3: MOTOR1.YELLOW, BREAKOUT1.YELLOW_wire
  N4: MOTOR1.PINK, BREAKOUT1.PINK_wire
  N5: MOTOR1.BLUE, BREAKOUT1.BLUE_wire
  N6: BREAKOUT1.In_1, Part1.D8
  N7: BREAKOUT1.In_2, Part1.D9_PWM
  N8: BREAKOUT1.In_3, Part1.D10_PWM/SS
  N9: BREAKOUT1.In_4, Part1.D11_PWM/MOSI
  N10: BREAKOUT1.0V, Part1.GND, U1.E, VCC1.-
  N11: BREAKOUT1.+5V, U1.A, VCC1.+
  N12: Part1.A0, U1.S

custom parts:
  ULN2003A breakout board: ULN2003A 7-way Darlington Transistor Driver on breakoutboard
