# Fritzing sketch Integrating the Infrared remote (saved by Fritzing 0.8.7b)
breadboards: 1

parts:
  LED1 = LED - 5mm [color="Red (633nm)" package="5 mm [THT]"]
  LED2 = LED - 5mm [color="Green (555nm)" package="5 mm [THT]"]
  LED3 = LED - 5mm [color="Orange (620nm)" package="5 mm [THT]"]
  LED4 = LED - 5mm [color="Blue (430nm)" package="5 mm [THT]"]
  Part1 = Arduino Uno (Rev3)
  R2 = Resistor [tolerance=±5% resistance=220 package=THT]
  R3 = Resistor [tolerance=±5% resistance=220 package=THT]
  R4 = Resistor [tolerance=±5% resistance=220 package=THT]
  R5 = Resistor [tolerance=±5% resistance=220 package=THT]
  IR1 = tl1838 [package=THT]

nets:
  N1: LED1.cathode, R4.Pin_0
  N2: LED1.anode, Part1.D12/MISO
  N3: LED2.cathode, R3.Pin_0
  N4: LED2.anode, Part1.D11_PWM/MOSI
  N5: LED3.cathode, R2.Pin_0
  N6: LED3.anode, Part1.D10_PWM/SS
  N7: LED4.cathode, R5.Pin_0
  N8: LED4.anode, Part1.D9_PWM
  N9: Part1.D4, IR1.OUT
  5V: Part1.5V, IR1.VCC
  GND: Part1.GND, R2.Pin_1, R3.Pin_1, R4.Pin_1, R5.Pin_1, IR1.GND

custom parts:
  tl1838: The TL1838 is a miniaturized receiver for infrared remote control systems. A PIN diode and a preamplifier are assembled on a lead frame, the epoxy package acts as an IR filter. The demodulated output signal can be directly decoded by a microprocessor.
