# Fritzing sketch Integrating a real time clock (saved by Fritzing 0.8.7b)
breadboards: 1

parts:
  Componente1 = Arduino Uno (Rev3)
  Convertitore_Expander_seriale = LCM1602 IIC [chip_label="Modulo " part_number="LCM1602 IIC" package="DIP (Dual Inline) [THT]"]
  U1 = LCD-16X2 [package=lcd-16x2]
  PCB2 = RTC_DS1302_module
  buz1 = Piezo Buzzer

nets:
  N1: Componente1.A4/SDA, Convertitore_Expander_seriale.SDA
  N2: Componente1.A5/SCL, Convertitore_Expander_seriale.SCL
  N3: Componente1.D8, PCB2.RST
  N4: Componente1.D5_PWM, buz1.pin_1
  N5: Componente1.D6_PWM, PCB2.CLK
  N6: Componente1.D7, PCB2.DAT
  VCC: Componente1.5V, Convertitore_Expander_seriale.VCC, PCB2.VCC
  GND: Componente1.GND, Convertitore_Expander_seriale.GND, PCB2.GND, buz1.pin_2
  VSS: Convertitore_Expander_seriale.VSS, U1.VSS
  VDD: Convertitore_Expander_seriale.VDD, U1.VDD
  N7: Convertitore_Expander_seriale.V0, U1.VO
  N8: Convertitore_Expander_seriale.RS, U1.RS
  N9: Convertitore_Expander_seriale.RW, U1.R_W
  N10: Convertitore_Expander_seriale.E, U1.E
  N11: Convertitore_Expander_seriale.D0, U1.DB0
  N12: Convertitore_Expander_seriale.D1, U1.DB1
  N13: Convertitore_Expander_seriale.D2, U1.DB2
  N14: Convertitore_Expander_seriale.D3, U1.DB3
  N15: Convertitore_Expander_seriale.D4, U1.DB4
  N16: Convertitore_Expander_seriale.D5, U1.DB5
  N17: Convertitore_Expander_seriale.D6, U1.DB6
  N18: Convertitore_Expander_seriale.D7, U1.DB7
  N19: Convertitore_Expander_seriale.A, U1.A
  N20: Convertitore_Expander_seriale.K, U1.K
  N21: Convertitore_Expander_seriale.LED_A, Convertitore_Expander_seriale.LED_B

custom parts:
  LCM1602 IIC: I2C-Module to use a 1602 or 2004 LCD on with the wire.h libory Serial LCD Modul
  RTC_DS1302_module: Arduino module DS1302 SPI Real Time Clock
  Piezo Buzzer: Part from https://www.nutsvolts.com/magazine/article/november2012_SmileysWorkshop modified to be .3 in spacing to match the adafruit buzzer 5V breadboard friendly part.
