# Fritzing sketch using the sn74hc595 shift register (saved by Fritzing 0.8.7b)
breadboards: 1

parts:
  U5 = 74HC595 [package="DIP16 [THT]"]
  Part1 = Arduino Uno (Rev3)
  LED1 = LED - 5mm [color="Red (633nm)" package="5 mm [THT]"]
  LED2 = LED - 5mm [color="Red (633nm)" package="5 mm [THT]"]
  LED3 = LED - 5mm [color="Red (633nm)" package="5 mm [THT]"]
  LED4 = LED - 5mm [color="Red (633nm)" package="5 mm [THT]"]
  LED5 = LED - 5mm [color="Red (633nm)" package="5 mm [THT]"]
  LED6 = LED - 5mm [color="Red (633nm)" package="5 mm [THT]"]
  LED7 = LED - 5mm [color="Red (633nm)" package="5 mm [THT]"]
  LED8 = LED - 5mm [color="Red (633nm)" package="5 mm [THT]"]
  R1 = Resistor [tolerance=±5% resistance=220 package=THT]
  R2 = Resistor [tolerance=±5% resistance=220 package=THT]
  R3 = Resistor [tolerance=±5% resistance=220 package=THT]
  R4 = Resistor [tolerance=±5% resistance=220 package=THT]
  R5 = Resistor [tolerance=±5% resistance=220 package=THT]
  R6 = Resistor [tolerance=±5% resistance=220 package=THT]
  R7 = Resistor [tolerance=±5% resistance=220 package=THT]
  R8 = Resistor [tolerance=±5% resistance=220 package=THT]

nets:
  N1: U5.Q1, LED1.anode
  N2: U5.Q2, LED2.anode
  N3: U5.Q3, LED3.anode
  N4: U5.Q4, LED4.anode
  N5: U5.Q5, LED5.anode
  N6: U5.Q6, LED6.anode
  N7: U5.Q7, LED7.anode
  GND: U5.GND, U5.OE, Part1.GND, R1.Pin_1, R2.Pin_1, R3.Pin_1, R4.Pin_1, R5.Pin_1, R6.Pin_1, R7.Pin_1, R8.Pin_1
  VCC: U5.MR, U5.VCC, Part1.5V
  N8: U5.SH_CP, Part1.D3_PWM
  N9: U5.ST_CP, Part1.D4
  N10: U5.DS, Part1.D2
  N11: U5.Q0, LED8.anode
  N12: LED1.cathode, R2.Pin_0
  N13: LED2.cathode, R3.Pin_0
  N14: LED3.cathode, R4.Pin_0
  N15: LED4.cathode, R5.Pin_0
  N16: LED5.cathode, R6.Pin_0
  N17: LED6.cathode, R7.Pin_0
  N18: LED7.cathode, R8.Pin_0
  N19: LED8.cathode, R1.Pin_0
